// Logisim project item_a.circ as structural Verilog
module d (
  input  A,
  input  B,
  input  C,
  output S
);

  wire and_1_out, not_1_out, undriven;

  not not_1 (not_1_out, A);
  and and_1 (and_1_out, not_1_out, undriven);
  or or_1 (S, and_1_out, C);
endmodule

module item_a (
  input  A,
  input  B,
  input  C,
  output S
);

  wire and_1_out, not_1_out;

  not not_1 (not_1_out, A);
  and and_1 (and_1_out, not_1_out, B);
  // NOT_Gate not_2: pin names not known
  or or_1 (S, and_1_out, C);
  // AND_Gate and_2 is placed but not wired
  // OR_Gate or_2 is placed but not wired
endmodule
