// Logisim project item_d.circ as structural Verilog
module cir_d (
  input  A,
  input  B,
  input  C,
  output X,
  output Y
);

  wire and_1_out, and_2_out, and_3_out;

  xor odd_parity_1 (X, A, B, C);
  and and_1 (and_1_out, A, B);
  and and_2 (and_2_out, B, C);
  or or_1 (Y, and_1_out, and_2_out, and_3_out);
  and and_3 (and_3_out, A, C);

  // Notes on the sheet:
  //   x = A ⊕ B ⊕ C
  //   ver tabela:
  //   projeto > analisar circuito
endmodule
