// Logisim project item_a.circ as structural Verilog: 2 circuits, main circuit main
module main (
  input  in_1,
  input  in_2,
  input  in_3,
  output out_4
);

  wire not_1_out, not_2_out, not_3_out, or_1_out;

  not not_1 (not_1_out, in_1);
  not not_2 (not_2_out, in_2);
  or or_1 (or_1_out, not_1_out, not_2_out);
  not not_3 (not_3_out, or_1_out);
  and and_1 (out_4, not_3_out, in_2, in_3);

  // Notes on the sheet:
  //   projeto > analisar circuito > tabela
  //   projeto > analisar circuito > minimizada
endmodule

module item_a_2 (
  input  A,
  input  B,
  input  C,
  output S
);

  wire nor_1_out, not_1_out, not_2_out;

  not not_1 (not_1_out, A);
  not not_2 (not_2_out, B);
  nor nor_1 (nor_1_out, not_1_out, not_2_out);
  and and_1 (S, nor_1_out, B, C);
endmodule
