// Logisim project item_a.circ as structural Verilog
module item_quest_3 (
  input  A,
  input  B,
  input  C,
  input  D,
  output S
);

  wire and_1_out, and_2_out, and_3_out, not_1_out, not_2_out, not_3_out, not_4_out, not_5_out;

  not not_1 (not_1_out, A);
  and and_1 (and_1_out, not_1_out, not_2_out);
  not not_2 (not_2_out, B);
  not not_3 (not_3_out, B);
  and and_2 (and_2_out, not_3_out, not_4_out);
  not not_4 (not_4_out, D);
  and and_3 (and_3_out, A, C, not_5_out);
  not not_5 (not_5_out, D);
  or or_1 (S, and_1_out, and_2_out, and_3_out);

  // Notes on the sheet:
  //   projeto > analisar circuito > minimizada
endmodule
