// Logisim project item_a.circ as structural Verilog
module Item_4 (
  input  T,
  input  U,
  input  H,
  input  F,
  output A
);

  wire and_1_out, and_2_out, and_3_out, and_4_out;

  and and_1 (and_1_out, T, H);
  and and_2 (and_2_out, F, U);
  and and_3 (and_3_out, U, T, F);
  and and_4 (and_4_out, U, T, H);
  or or_1 (A, and_1_out, and_2_out, and_3_out, and_4_out);

  // Notes on the sheet:
  //   projeto > analisar circuito > tabela
  //   projeto > analisar circuito > minimizada
endmodule
