// Logisim project item_a.circ as structural Verilog
module questao_5 (
  input  B2,
  input  B1,
  input  B0,
  output y3,
  output y2,
  output y1,
  output y0
);

  wire and_3_out, and_4_out, and_5_out, not_1_out, not_2_out, not_3_out;

  not not_1 (not_1_out, B2);
  not not_2 (not_2_out, B1);
  not not_3 (not_3_out, B0);
  and and_1 (y3, B2, B1);
  and and_2 (y2, B2, not_2_out);
  and and_3 (and_3_out, not_1_out, not_2_out, not_3_out);
  and and_4 (and_4_out, B1, B0);
  and and_5 (and_5_out, B2, B0);
  or or_1 (y1, and_3_out, and_4_out, and_5_out);

  assign y0 = 1'b1;

  // Notes on the sheet:
  //   projeto > analisar circuito > tabela
  //   projeto > analisar circuito > minimizada
endmodule
